# Fritzing sketch geekshield_v12 (saved by Fritzing 0.9.5d)
circuit board: 7.18cm x 5.58cm

parts:
  ESP32-CAM = ESP32 - CAM
  POWERBTN = Pololu Power Switch-LV
  SERVO_PWM = female pin header, 5 pins [form="♀ (female)"]
  SERVO_GND = female pin header, 5 pins [form="♀ (female)"]
  SERVO_VIN = female pin header, 5 pins [form="♀ (female)"]
  Pad1 = Pad [width=3 height=1.5 connect=center]
  Pad2 = Pad [width=3 height=1.5 connect=center]
  Pad3 = Pad [width=3 height=1.5 connect=center]
  Pad4 = Pad [width=3 height=1.5 connect=center]
  Pad5 = Pad [width=3 height=1.5 connect=center]
  Pad6 = Pad [width=3 height=1.5 connect=center]
  Pad7 = Pad [width=3 height=1.5 connect=center]
  Pad8 = Pad [width=3 height=1.5 connect=center]
  R2 = Resistor [tolerance=±5% resistance=4.7k package=THT]
  R1 = Resistor [tolerance=±5% resistance=2.2k package=THT]
  UART0 = female pin header, 3 pins [form="♀ (female)"]
  VREG = female pin header, 3 pins [form="♀ (female)"]
  DRV8835 = DRV8835 Dual Motor Driver Carrier
  Pad9 = Pad [width=3 height=1.5 connect=center]
  Pad10 = Pad [width=3 height=1.5 connect=center]
  AUXBTN = Mini Pushbutton
  EXTPOWER = female pin header, 1 pin [form="♀ (female)"]  # not connected

nets:
  MOTOR_A V+/MOTOR_B V+: ESP32-CAM.5V, POWERBTN.VOUT, SERVO_VIN.pin1, SERVO_VIN.pin2, SERVO_VIN.pin3, SERVO_VIN.pin4, SERVO_VIN.pin5, Pad2.pad, Pad5.pad, R2.Pin_1, VREG.pin1, VREG.pin3, DRV8835.VIN
  BAT-/MOTOR_A GND/MOTOR_B GND: ESP32-CAM.GND, POWERBTN.GND, SERVO_GND.pin1, SERVO_GND.pin2, SERVO_GND.pin3, SERVO_GND.pin4, SERVO_GND.pin5, Pad4.pad, Pad8.pad, R1.Pin_1, UART0.pin3, VREG.pin2, DRV8835.GND, DRV8835.GND-13, Pad10.pad, AUXBTN.leg1
  N1: ESP32-CAM.IO12, SERVO_PWM.pin4, DRV8835.BIN2/BENABLE
  N2: ESP32-CAM.IO13, SERVO_PWM.pin3, DRV8835.BIN1/BPHASE
  N3: ESP32-CAM.IO15, SERVO_PWM.pin2, DRV8835.AIN2/AENABLE
  N4: ESP32-CAM.IO14, SERVO_PWM.pin1, DRV8835.AIN1/APHASE
  N5: ESP32-CAM.IO2, POWERBTN.OFF
  N6: ESP32-CAM.VOT, UART0.pin2
  N7: ESP32-CAM.VOR, UART0.pin1
  VCC: ESP32-CAM.VCC, DRV8835.VCC
  N8: ESP32-CAM.IO0, R2.Pin_0, R1.Pin_0, AUXBTN.leg0
  N9: ESP32-CAM.IO16, SERVO_PWM.pin5
  BAT+: POWERBTN.VIN, Pad9.pad
  MOTOR_A C2: Pad1.pad, DRV8835.AOUT1
  MOTOR_A C1: Pad3.pad, DRV8835.AOUT2
  MOTOR_B C2: Pad6.pad, DRV8835.BOUT1
  MOTOR_B C1: Pad7.pad, DRV8835.BOUT2

notes:
  JUMPER FOR 5V
  V+ GND 5V
  GND TX RX
  ___
  V+
  C2
  C1
  GND
  B+
  B-
  ~
  5
  -
  +
  A
  B
  -GND-
  1
  2
  3
  4
  GeekShield v1.2
  JLCJLCJLCJLC
  VIN
  VOUT (5V)
  VCC ->
  3.3V ->
  <- 5V

custom parts:
  ESP32 - CAM: The ESP32-CAM has a very competitive small-size camera module that can operate independently as a minimum system with a footprint of only 27*40.5*4.5mm and a deep sleep current of up to 6mA.
  Pololu Power Switch-LV: Mini Pushbutton Power Switch with Reverse Voltage Protection, LV
  Mini Pushbutton: A small pushbutton
